# Fritzing sketch Burg (saved by Fritzing 1.0.4)
circuit board: 32.9196cm x 32.7948cm
breadboards: 1

parts:
  esp1 = ESP32 DevKitc V4
  WTV020-SD1 = WTV020-SD [part_number=WTV020-SD]
  Bauteil1 = Adafruit PCA9685 PWM/Servo Breakout [part_number=815]

nets:
  N1: esp1.IO21, Bauteil1.SDA
  N2: esp1.IO22, Bauteil1.SCL
  GND: esp1.GND, Bauteil1.GND
  5V: esp1.5V, Bauteil1.5.0V, Bauteil1.VCC
  N3: WTV020-SD1.SPK+, WTV020-SD1.P05

custom parts:
  ESP32 DevKitc V4: ESP32-DevKitC board with ESP32-WROOM-32 module. ESP32-DevKitC V4 is a small-sized ESP32-based development board produced by Espressif. Most of the pins on the ESP module are broken out to the pin headers on the board. The pins D0, D1, D2, D3, CMD and CLK are used internally for communication between ESP32 and SPI flash memory. They are grouped on both sides near the USB connector. Avoid using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
  Adafruit PCA9685 PWM/Servo Breakout: Using only two pins, control 16 free-running PWM outputs! I2C-controlled PWM driver with a built in clock. Unlike the TLC5940 family, you do not need to continuously send it signal tying up your microcontroller, its completely free running! 5V compliant, which means you can control it from a 3.3V microcontroller and still safely drive up to 6V outputs (this is good for when you want to control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
