# Fritzing sketch Grill (saved by Fritzing 1.0.4)

parts:
  ESP = ESP32 DevKitc V4
  C1 = Capacitor Polarized [part_number="1000 µF" package=panasonic_e]
  WTV020-SD1 = WTV020-SD [part_number=WTV020-SD]
  SPKR1 = Loudspeaker
  R1 = Resistor [tolerance=±5% resistance=470 package="2512 [SMD]"]
  R2 = Resistor [tolerance=±5% power=0.25W resistance=100 package=THT]
  R3 = Resistor [tolerance=±5% power=0.25W resistance=220 package=THT]  # not connected
  R4 = Resistor [tolerance=±5% power=0.25W resistance=100 package=THT]
  LED1 = LED - 5mm [color="Red (633nm)" current=0.030A package="5 mm [THT]"]
  LED2 = LED - 5mm [color="White (6500K)" current=0.030A package="5 mm [THT]"]
  Bauteil1 = Adafruit MicroSD card breakout board [part_number="Adafruit #254"]  # not connected
  Neopixel-Ring = 12 NeoPixel Ring [part_number=1643]

nets:
  N1: ESP.CLK, WTV020-SD1.P04
  N2: ESP.D0, WTV020-SD1.P05
  N3: ESP.IO2, R1.Pin_0
  N4: ESP.GND#12, WTV020-SD1.GND
  VDD: ESP.3V3, C1.+, WTV020-SD1.VDD, Neopixel-Ring.VDD
  N5: ESP.IO25, R2.Pin_0
  N6: ESP.IO26, R4.Pin_1
  N7: ESP.GND#32, C1.-, LED1.cathode, LED2.cathode
  N8: WTV020-SD1.SPK+, SPKR1.pin1
  N9: WTV020-SD1.SPK-, SPKR1.pin2
  N10: R2.Pin_1, LED2.anode
  N11: R4.Pin_0, LED1.anode

custom parts:
  ESP32 DevKitc V4: ESP32-DevKitC board with ESP32-WROOM-32 module. ESP32-DevKitC V4 is a small-sized ESP32-based development board produced by Espressif. Most of the pins on the ESP module are broken out to the pin headers on the board. The pins D0, D1, D2, D3, CMD and CLK are used internally for communication between ESP32 and SPI flash memory. They are grouped on both sides near the USB connector. Avoid using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
  Adafruit MicroSD card breakout board: Not just a simple breakout board, this microSD adapter goes the extra mile - designed for ease of use. Onboard 5v->3v regulator provides 150mA for power-hungry cards 3v level shifting means you can use this with ease on either 3v or 5v systems Uses a proper level shifting chip, not resistors: less problems, and faster read/write access Use 3 or 4 digital pins to read and write 2Gb+ of storage!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
  12 NeoPixel Ring: 12 ultra bright smart LED NeoPixels are arranged in a circle with 1.5" (37mm) outer diameter. The rings are 'chainable' - connect the output pin of one to the input pin of another. Use only one microcontroller pin to control as many as you can chain together! Each LED is addressable as the driver chip is inside the LED. Each one has ~18mA constant current drive so the color will be very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
