# Fritzing sketch Bahnstrom (saved by Fritzing 0.9.3b)
breadboards: 1

parts:
  J1 = screw terminal, 12 pins
  J2 = screw terminal, 12 pins

nets:
  Gleis 13: J1.pin1
  Gleis 12: J1.pin2
  Gleis 2: J1.pin3
  Gleis 1: J1.pin4
  Außen: J1.pin5
  Innen: J1.pin6
  Gleis 11: J1.pin7
  Ausfahrt: J1.pin8
  Schiene: J1.pin9, J1.pin10, J1.pin11, J1.pin12
  N1: J2.pin9, J2.pin10, J2.pin11, J2.pin12
